// Logisim project Regfile.circ as structural Verilog: 1 circuit, main circuit main
module main (
  input  [1:0] Read_register_1,
  input  [1:0] Read_register_2,
  input  [1:0] write_register,
  input  [15:0] write_data,
  input  RegWrite,
  input  clock,
  output [15:0] Reg_0_Value,
  output [15:0] Reg_1_Value,
  output [15:0] Reg_2_Value,
  output [15:0] Reg_3_Value,
  output [15:0] Read_Data_1,
  output [15:0] Read_Data_2
);

  wire demultiplexer_1_out0, demultiplexer_1_out1, demultiplexer_1_out2, demultiplexer_1_out3;
  wire [15:0] multiplexer_1_out, multiplexer_2_out, multiplexer_3_out, multiplexer_4_out;

  Register #(.width(16)) register_1 (.D(multiplexer_1_out), .Q(Reg_0_Value), .clk(clock));  // open: en, clr
  Multiplexer #(.width(16)) multiplexer_1 (
    .in0(Reg_0_Value), .in1(write_data), .out(multiplexer_1_out), .sel(demultiplexer_1_out0));  // open: en
  Demultiplexer #(.select(2)) demultiplexer_1 (
    .out0(demultiplexer_1_out0), .out1(demultiplexer_1_out1), .out2(demultiplexer_1_out2),
    .out3(demultiplexer_1_out3), .in(RegWrite), .sel(write_register));  // open: en
  Multiplexer #(.width(16)) multiplexer_2 (
    .in0(Reg_1_Value), .in1(write_data), .out(multiplexer_2_out), .sel(demultiplexer_1_out1));  // open: en
  Register #(.width(16)) register_2 (.D(multiplexer_2_out), .Q(Reg_1_Value), .clk(clock));  // open: en, clr
  Multiplexer #(.width(16)) multiplexer_3 (
    .in0(Reg_2_Value), .in1(write_data), .out(multiplexer_3_out), .sel(demultiplexer_1_out2));  // open: en
  Register #(.width(16)) register_3 (.D(multiplexer_3_out), .Q(Reg_2_Value), .clk(clock));  // open: en, clr
  Multiplexer #(.width(16)) multiplexer_4 (
    .in0(Reg_3_Value), .in1(write_data), .out(multiplexer_4_out), .sel(demultiplexer_1_out3));  // open: en
  Register #(.width(16)) register_4 (.D(multiplexer_4_out), .Q(Reg_3_Value), .clk(clock));  // open: en, clr
  Multiplexer #(.select(2), .width(16)) multiplexer_5 (
    .in0(Reg_0_Value), .in1(Reg_1_Value), .in2(Reg_2_Value), .in3(Reg_3_Value), .out(Read_Data_1),
    .sel(Read_register_1));  // open: en
  Multiplexer #(.select(2), .width(16)) multiplexer_6 (
    .in0(Reg_0_Value), .in1(Reg_1_Value), .in2(Reg_2_Value), .in3(Reg_3_Value), .out(Read_Data_2),
    .sel(Read_register_2));  // open: en
endmodule
